// Logisim project k16x.circ as structural Verilog: 1 circuit, main circuit main
module main (
);

  wire ALUCarryIn, IOWe, not_1_out, or_1_out, RST;
  wire [3:0] ALUOp;
  wire [15:0] adder_1_out, ALUOut, demultiplexer_1_out0, demultiplexer_1_out1, demultiplexer_1_out2,
       demultiplexer_1_out3, demultiplexer_1_out4, demultiplexer_1_out5, demultiplexer_1_out6,
       demultiplexer_1_out7, IMMHi, IMMLo, Instruction, IOIn, IOOut, pc_q, RegAOut, RegBOut, RegIn, sp_q,
       subtractor_1_out, x0_q, x1_q, x2_q, x3_q, x4_q, x5_q;
  wire [31:0] bit_extender_1_out, IOAddr;

  // Probe on RegAOut
  Multiplexer #(.select(3), .width(16)) multiplexer_1 (
    .in0(x0_q), .in1(x1_q), .in2(x2_q), .in3(x3_q), .in4(x4_q), .in5(x5_q), .in6(sp_q), .in7(pc_q),
    .out(RegAOut), .sel(Instruction[2:0]));
  // Probe on RegBOut
  Multiplexer #(.select(3), .width(16)) multiplexer_2 (
    .in0(x0_q), .in1(x1_q), .in2(x2_q), .in3(x3_q), .in4(x4_q), .in5(x5_q), .in6(sp_q), .in7(pc_q),
    .out(RegBOut), .sel(Instruction[5:3]));
  Register #(.width(16)) u_Instruction (
    .D(IOOut), .Q({Instruction[15:10], ALUOp, Instruction[5:0]}), .clr(RST));  // open: en, clk
  Button Reset (.out(RST));
  Register #(.width(16)) x0 (.D(demultiplexer_1_out0), .en(Instruction[12]), .Q(x0_q), .clr(RST));  // open: clk
  Register #(.width(16)) x1 (.D(demultiplexer_1_out1), .en(Instruction[12]), .Q(x1_q), .clr(RST));  // open: clk
  Register #(.width(16)) u_IMMLo (.D(IOOut), .Q(IMMLo), .clr(RST));  // open: en, clk
  Register #(.width(16)) x2 (.D(demultiplexer_1_out2), .en(Instruction[12]), .Q(x2_q), .clr(RST));  // open: clk
  Register #(.width(16)) x3 (.D(demultiplexer_1_out3), .en(Instruction[12]), .Q(x3_q), .clr(RST));  // open: clk
  Register #(.width(16)) u_IMMHi (.D(IOOut), .Q(IMMHi), .clr(RST));  // open: en, clk
  assign bit_extender_1_out = {{16{1'b0}}, RegBOut};  // Bit_Extender bit_extender_1
  Register #(.width(16)) x4 (.D(demultiplexer_1_out4), .en(Instruction[12]), .Q(x4_q), .clr(RST));  // open: clk
  Multiplexer #(.width(32)) multiplexer_3 (
    .in0({IMMHi, IMMLo}), .in1(bit_extender_1_out), .out(IOAddr), .sel(Instruction[15]));
  Register #(.width(16)) x5 (.D(demultiplexer_1_out5), .en(Instruction[12]), .Q(x5_q), .clr(RST));  // open: clk
  Register #(.width(16)) sp (.D(demultiplexer_1_out6), .en(Instruction[12]), .Q(sp_q), .clr(RST));  // open: clk
  not not_1 (not_1_out, Instruction[12]);
  or or_1 (or_1_out, Instruction[13], Instruction[14]);
  Register #(.width(16)) pc (.D(demultiplexer_1_out7), .en(Instruction[12]), .Q(pc_q), .clr(RST));  // open: clk
  Multiplexer #(.enable("true"), .select(2), .width(16)) multiplexer_4 (
    .in0(ALUOut), .in1(RegBOut), .in2(ALUOut), .in3(IMMLo), .out(RegIn), .sel(Instruction[14:13]),
    .en(Instruction[12]));
  Multiplexer #(.enable("true"), .select(2), .width(16)) multiplexer_5 (
    .in1(RegAOut), .in2(ALUOut), .in3(IMMLo), .out(IOIn), .sel(Instruction[14:13]), .en(IOWe));  // open: in0
  and and_1 (IOWe, not_1_out, or_1_out);
  Demultiplexer #(.select(3), .width(16)) demultiplexer_1 (
    .out0(demultiplexer_1_out0), .out1(demultiplexer_1_out1), .out2(demultiplexer_1_out2),
    .out3(demultiplexer_1_out3), .out4(demultiplexer_1_out4), .out5(demultiplexer_1_out5),
    .out6(demultiplexer_1_out6), .out7(demultiplexer_1_out7), .in(RegIn), .sel(Instruction[2:0]));
  Adder #(.width(16)) adder_1 (.a(RegAOut), .b(RegBOut), .out(adder_1_out), .cin(ALUCarryIn));  // open: cout
  Subtractor #(.width(16)) subtractor_1 (
    .a(RegAOut), .b(RegBOut), .out(subtractor_1_out), .bin(ALUCarryIn));  // open: bout
  // Probe on ALUOut
  Multiplexer #(.select(4), .width(16)) multiplexer_6 (
    .in0(adder_1_out), .in1(subtractor_1_out), .out(ALUOut), .sel(ALUOp));  // open: in2, in3, in4, in5, in6, in7, in8, in9, in10, in11, in12, in13, in14, in15

  // Other names for the same wires on the sheet: RegASelect[2:0] = Instruction[2:0];
  //   RegBSelect[2:0] = Instruction[5:3]; Instruction[9:6] = ALUOp; RegWE = Instruction[12];
  //   WriteSelect[2:0] = Instruction[14:12]; IOAddrSelect = Instruction[15]
endmodule
